# Fritzing sketch Control Surface Prototype (saved by Fritzing 0.9.5d)
breadboards: 2

parts:
  S1 = Pushbutton [package="[THT]"]
  S2 = Momentary Switch [package=ksa_sealed_tac_switch]  # not connected
  S3 = Momentary Switch [package=ksa_sealed_tac_switch]  # not connected
  S4 = Momentary Switch [package=ksa_sealed_tac_switch]  # not connected
  R1 = Rotary Potentiometer (Small) [maximum_resistance=100kΩ package=THT]  # not connected
  R2 = Rotary Potentiometer (Small) [maximum_resistance=100kΩ package=THT]
  R3 = Slide Potentiometer [maximum_resistance=100kΩ]  # not connected
  Grove1 = Grove OLED 128x96  # not connected
  CPU1 = NodeMCU WROOM ESP 32
  S5 = Pushbutton [package="[THT]"]
  S6 = Momentary Switch [package=ksa_sealed_tac_switch]
  S7 = Momentary Switch [package=ksa_sealed_tac_switch]  # not connected
  S8 = Momentary Switch [package=ksa_sealed_tac_switch]  # not connected
  U1 = ENCODER-QUADRATURE [package=encoder-16mm-quad]  # not connected
  Grove2 = Grove OLED 128x96  # not connected
  R4 = Slide Potentiometer [maximum_resistance=100kΩ]  # not connected
  S11 = Pushbutton [package="[THT]"]
  S12 = Pushbutton [package="[THT]"]
  S13 = Pushbutton [package="[THT]"]
  S14 = Pushbutton [package="[THT]"]
  R5 = Rotary Potentiometer (Small) [maximum_resistance=100kΩ package=THT]  # not connected
  R6 = Rotary Potentiometer (Small) [maximum_resistance=100kΩ package=THT]  # not connected
  R7 = Slide Potentiometer [maximum_resistance=100kΩ]  # not connected
  Part2 = Arduino Nano (Rev3.0) (ICSP)  # not connected
  U2 = Thumb Joystick [package=joystick]  # not connected

nets:
  N1: S1.Pin_1, S1.Pin_2
  N2: S1.Pin_3, S1.Pin_4
  N3: R2.leg1, CPU1.pin_7
  N4: R2.leg2, CPU1.pin_5
  N5: CPU1.pin_8, CPU1.pin_24, CPU1.pin_28
  N6: CPU1.pin_9, CPU1.pin_25
  N7: S5.Pin_1, S5.Pin_2
  N8: S5.Pin_3, S5.Pin_4
  N9: S6.1, S6.2
  N10: S6.3, S6.4
  N11: S11.Pin_1, S11.Pin_2
  N12: S11.Pin_3, S11.Pin_4
  N13: S12.Pin_1, S12.Pin_2
  N14: S12.Pin_3, S12.Pin_4
  N15: S13.Pin_1, S13.Pin_2
  N16: S13.Pin_3, S13.Pin_4
  N17: S14.Pin_1, S14.Pin_2
  N18: S14.Pin_3, S14.Pin_4

custom parts:
  NodeMCU WROOM ESP 32: 30 pol Development Kit
